# Fritzing sketch minipGateGuard (saved by Fritzing 0.9.3b)
breadboards: 1

parts:
  IOXESP32PS1 = IOXESP32PS [part_number=IOXESP32 chip_label=IOXESP32PS package="DIP (Dual Inline) [THT]"]
  Part1 = RFID-RC522-v2
  J1 = Basic Servo

nets:
  3V3: IOXESP32PS1.3V3, Part1.3.3V
  N1: IOXESP32PS1.IO26, J1.pulse
  N2: IOXESP32PS1.GND#13, J1.gnd
  5V: IOXESP32PS1.5V, J1.vcc
  N3: IOXESP32PS1.IO0, Part1.RST
  N4: IOXESP32PS1.IO5, Part1.SDA
  N5: IOXESP32PS1.IO18, Part1.SCK
  N6: IOXESP32PS1.IO19, Part1.MISO
  N7: IOXESP32PS1.GND#49, Part1.GND
  N8: IOXESP32PS1.IO22, Part1.MOSI

custom parts:
  IOXESP32PS: ESP32 Development board By IOXhop
  RFID-RC522-v2: A simple China made RFID-RC522 Reader; do check the pin labels, as this is a MFRC522 based clone.
